# Fritzing sketch Untitled Sketch (saved by Fritzing 0.9.10b)

parts:
  Part1 = Arduino Uno (Rev3) - ICSP
  Mod1 = Raspberry Pi Pico
  Part2 = TXB0108 8-channel Bi-directional Logic Level Converter

nets:
  N1: Part1.D0/RX, Part2.B2
  N2: Part1.D1/TX, Part2.B1
  N3: Part1.5V, Part2.VCCB
  GND: Part1.GND, Mod1.pin_8, Mod1.pin_33, Part2.GND
  N4: Mod1.pin_1, Part2.A2
  N5: Mod1.pin_2, Part2.A1
  N6: Mod1.pin_36, Part2.OE, Part2.VCCA

custom parts:
  Raspberry Pi Pico: Raspberry Pi Pico. Based around the RP2040 microcontroller the Pico is a low cost microcontroller device bringing Raspberry Pi quality, cost, and easy of use to the microcontroller space. Jan 2021, Split part in to two versions: tht (this one) and SMD. This one will drill holes for a .1 in header in pcb to allow plugging in the module as well as providing pads to solder the module to the top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
  TXB0108 8-channel Bi-directional Logic Level Converter: Because the Arduino (and Basic Stamp) are 5V devices, and most modern sensors, displays, flash cards and modes are 3.3V-only, many makers find that they need to perform level shifting/conversion to protect the 3.3V device from 5V. Although one can use resistors to make a divider, for high speed transfers, the resistors can add a lot of slew and cause havoc that is tough to debug. For that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
